# Fritzing sketch ButtonsBuzzerLEDSketch (saved by Fritzing 0.9.6b)
breadboards: 1

parts:
  Part1 = Arduino Mega 2560 (Rev3)
  LED1 = LED - 3mm [color="Red (633nm)" current=0.030 package="3 mm [THT]"]
  LED2 = smd LED [color="Red (633nm)" package="0805 [SMD]"]
  R1 = Resistor [tolerance=±5% resistance=220 package="0805 [SMD]"]
  R2 = Resistor [tolerance=±5% resistance=220 package="0805 [SMD]"]
  S1 = Momentary Switch [package=ksa_sealed_tac_switch]
  S2 = Momentary Switch [package=ksa_sealed_tac_switch]
  S3 = Momentary Switch [package=ksa_sealed_tac_switch]
  SG1 = Buzzer 12mm [package=buzzer-ccv]

nets:
  N1: Part1.GND, LED1.cathode, LED2.cathode, S1.1, S2.1, S3.1, SG1.2
  N2: Part1.D12_PWM, R1.Pin_1
  N3: Part1.D11_PWM, R2.Pin_1
  N4: Part1.D2_PWM, S3.4
  N5: Part1.D3_PWM, SG1.1
  N6: Part1.D4_PWM, S2.4
  N7: Part1.D5_PWM, S1.4
  N8: LED1.anode, R2.Pin_0
  N9: LED2.anode, R1.Pin_0
